// Logisim project Lab1_computadores.circ as structural Verilog: 4 circuits, main circuit main
module main (
  input  in_1,
  input  in_2,
  input  in_3,
  output out_4,
  output out_5
);

  Sumador sumador_1 (.A(in_2), .B(in_3), .Cin(in_1), .S(out_4), .Cout(out_5));
  Sumador_overflow sumador_overflow_1 ();  // open: A, B, Cin, S, Cout, Overflow
endmodule

module Sumador (
  input  A,
  input  B,
  input  Cin,
  output S,
  output Cout
);

  wire and_1_out, and_2_out, and_3_out, and_4_out, and_5_out, and_6_out, and_7_out, not_1_out, not_2_out,
       not_3_out, not_4_out, not_5_out, not_6_out;

  not not_1 (not_1_out, A);
  not not_2 (not_2_out, B);
  not not_3 (not_3_out, A);
  not not_4 (not_4_out, Cin);
  not not_5 (not_5_out, B);
  not not_6 (not_6_out, Cin);
  and and_1 (and_1_out, B, Cin);
  and and_2 (and_2_out, A, Cin);
  and and_3 (and_3_out, A, B);
  and and_4 (and_4_out, not_1_out, not_2_out, Cin);
  and and_5 (and_5_out, not_3_out, B, not_4_out);
  and and_6 (and_6_out, A, not_5_out, not_6_out);
  and and_7 (and_7_out, A, B, Cin);
  or or_1 (Cout, and_1_out, and_2_out, and_3_out);
  or or_2 (S, and_4_out, and_5_out, and_6_out, and_7_out);
endmodule

module Sumador_overflow (
  input  A,
  input  B,
  input  Cin,
  output S,
  output Cout,
  output Overflow
);

  wire and_1_out, and_2_out, and_3_out, and_4_out, and_5_out, and_6_out, and_7_out, and_8_out, and_9_out,
       not_1_out, not_2_out, not_3_out, not_4_out, not_5_out, not_6_out, not_7_out;

  not not_1 (not_1_out, A);
  not not_2 (not_2_out, B);
  not not_3 (not_3_out, A);
  not not_4 (not_4_out, Cin);
  not not_5 (not_5_out, B);
  not not_6 (not_6_out, Cin);
  and and_1 (and_1_out, B, Cin);
  and and_2 (and_2_out, A, Cin);
  and and_3 (and_3_out, A, B);
  and and_4 (and_4_out, not_1_out, not_2_out, Cin);
  and and_5 (and_5_out, not_3_out, B, not_4_out);
  and and_6 (and_6_out, A, not_5_out, not_6_out);
  and and_7 (and_7_out, A, B, Cin);
  or or_1 (Cout, and_1_out, and_2_out, and_3_out);
  not not_7 (not_7_out, Cout);
  or or_2 (S, and_4_out, and_5_out, and_6_out, and_7_out);
  and and_8 (and_8_out, not_7_out, Cin);
  and and_9 (and_9_out, not_6_out, Cout);
  or or_3 (Overflow, and_8_out, and_9_out);
endmodule

module ALU_bit_1 (
  input  A,
  input  B,
  input  Cint,
  input  [2:0] Op,
  output out_5,
  output out_6
);

  wire and_1_out, nor_1_out, nor_2_out, or_1_out, sumador_1_cout, sumador_1_s, sumador_2_cout, sumador_2_s;

  nor nor_1 (nor_1_out, B, B);
  and and_1 (and_1_out, B, A);
  or or_1 (or_1_out, B, A);
  nor nor_2 (nor_2_out, B, A);
  Sumador sumador_1 (.A(A), .B(B), .Cin(Cint), .S(sumador_1_s), .Cout(sumador_1_cout));
  Sumador sumador_2 (.A(B), .B(nor_1_out), .Cin(Cint), .S(sumador_2_s), .Cout(sumador_2_cout));
  Multiplexer #(.select(3), .enable("false")) multiplexer_1 (
    .in0(and_1_out), .in1(sumador_2_s), .in3(sumador_1_s), .in4(nor_2_out), .in6(or_1_out), .out(out_5),
    .sel(Op));  // open: in2, in5, in7
  Multiplexer #(.select(3), .enable("false")) multiplexer_2 (
    .in1(sumador_2_cout), .in3(sumador_1_cout), .out(out_6), .sel(Op));  // open: in0, in2, in4, in5, in6, in7
endmodule
